# Fritzing sketch analog_sensors (saved by Fritzing 0.9.3b)
breadboards: 1

parts:
  T-Cobbler1 = T-Cobbler
  U1 = TMP36 [part_number=TMP36 package=to-92]
  IC1 = IC, DIP package, 8 pins [chip_label=3002]
  R1 = Photocell (LDR) [package=THT]
  R2 = Resistor [tolerance=±5% resistance=10k package=THT]
  LED1 = LED - 5mm [color="White (4500K)" package="5 mm [THT]"]
  LED2 = LED - 5mm [color="Red (635nm)" package="5 mm [THT]"]
  R3 = Resistor [tolerance=±5% resistance=220 package=THT]
  R4 = Resistor [tolerance=±5% resistance=220 package=THT]

nets:
  N1: T-Cobbler1.3V3#0, U1.VCC, IC1.pin8, R1.pin_0
  N2: T-Cobbler1.GPIO17, LED1.anode
  N3: T-Cobbler1.GPIO27, LED2.anode
  N4: T-Cobbler1.SPIMOSI, IC1.pin5
  N5: T-Cobbler1.SPIMISO, IC1.pin6
  N6: T-Cobbler1.SPISCLK, IC1.pin7
  N7: T-Cobbler1.GND#26, U1.GND, IC1.pin4, R2.Pin_1, R3.Pin_1, R4.Pin_1
  N8: T-Cobbler1.SPICE0, IC1.pin1
  N9: U1.VOUT, IC1.pin2
  N10: IC1.pin3, R1.pin_1, R2.Pin_0
  N11: LED1.cathode, R3.Pin_0
  N12: LED2.cathode, R4.Pin_0

custom parts:
  T-Cobbler: T-Cobbler for RPi B+ and Rpi2 from SunFounder
