# Fritzing sketch binary_display (saved by Fritzing 0.9.3b)
breadboards: 1

parts:
  Part1 = Adafruit T-Cobbler Plus [part_number="Adafruit #1989 and #2028"]
  LED1 = LEDs [package=led10mm]
  LED2 = LEDs [package=led10mm]
  LED3 = LEDs [package=led10mm]
  LED4 = LEDs [package=led10mm]
  R1 = Resistor [tolerance=±5% resistance=470 package=THT]
  R2 = Resistor [tolerance=±5% resistance=470 package=THT]
  R3 = Resistor [tolerance=±5% resistance=470 package=THT]
  R4 = Resistor [tolerance=±5% resistance=470 package=THT]
  LED5 = LEDs [package=led10mm]
  R5 = Resistor [tolerance=±5% resistance=470 package=THT]

nets:
  N1: Part1.GND, R1.Pin_1, R2.Pin_1, R3.Pin_1, R4.Pin_1, R5.Pin_1
  N2: Part1.GPIO17, LED5.A
  N3: Part1.GPIO27, LED1.A
  N4: Part1.GPIO22, LED2.A
  N5: Part1.GPIO13, LED3.A
  N6: Part1.GPIO19, LED4.A
  N7: LED1.C, R1.Pin_0
  N8: LED2.C, R2.Pin_0
  N9: LED3.C, R3.Pin_0
  N10: LED4.C, R4.Pin_0
  N11: LED5.C, R5.Pin_0

custom parts:
  Adafruit T-Cobbler Plus: The Raspberry Pi has landed on the Maker World like a 40-GPIO pinned, quad-USB ported, credit card sized bomb of DIY joy. And while you can use most of our great Model B accessories by hooking up our downgrade cable, its probably a good time to upgrade your set up and accessorize using all of the 40 pins. That's why we now carry the Assembled Adafruit Pi T-Cobbler Plus - Breakout + Cable for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
